# Fritzing sketch Musical Instruments (saved by Fritzing 0.9.3b)
breadboards: 1

parts:
  hc-sr1 = hc-sr04
  R1 = Basic Flex Resistor
  R2 = Resistor [tolerance=±5% resistance=220 package=THT]
  R3 = Photocell (LDR) [package=THT]
  R4 = Resistor [tolerance=±5% resistance=220 package=THT]
  J1 = Piezo Speaker
  Part2 = Arduino Uno (Rev3)

nets:
  VCC: hc-sr1.VCC, R2.Pin_1, R3.pin_0, J1.pin1, Part2.5V
  N1: hc-sr1.Trig, Part2.D7
  N2: hc-sr1.Echo, Part2.D2
  GND: hc-sr1.GND, R1.pin_1, R4.Pin_1, J1.pin2, Part2.GND
  N3: R1.Pin_2, R2.Pin_0, Part2.A0
  N4: R3.pin_1, R4.Pin_0, Part2.A1
